# Fritzing sketch Raspberry_Sketch (saved by Fritzing 0.9.1b)

parts:
  Raspberry_Pi1 = Raspberry Pi B+
  LED1 = RGB LED (com. cathode, rgb) [package="5 mm [THT]"]
  LED2 = RGB LED (com. cathode, rgb) [package="5 mm [THT]"]
  S1 = Pushbutton [package="[THT]"]
  S2 = Pushbutton [package="[THT]"]
  S3 = Pushbutton [package="[THT]"]
  S4 = Pushbutton [package="[THT]"]
  Bauteil1 = LilyPad Light Sensor
  U1 = VCNL4000 [package=vcnl4000]
  Q1 = PNP-Transistor [package="TO92 [THT]"]
  Q2 = PNP-Transistor [package="TO92 [THT]"]
  Q3 = PNP-Transistor [package="TO92 [THT]"]
  Q4 = PNP-Transistor [package="TO92 [THT]"]
  Q5 = PNP-Transistor [package="TO92 [THT]"]
  Q6 = PNP-Transistor [package="TO92 [THT]"]
  R1 = Resistor [tolerance=±5% resistance=220 package=THT]
  R2 = Resistor [tolerance=±5% resistance=220 package=THT]
  R3 = Resistor [tolerance=±5% resistance=220 package=THT]
  R4 = Resistor [tolerance=±5% resistance=220 package=THT]
  R5 = Resistor [tolerance=±5% resistance=220 package=THT]
  R6 = Resistor [tolerance=±5% resistance=220 package=THT]
  R7 = Resistor [tolerance=±5% resistance=220 package=THT]
  R8 = Resistor [tolerance=±5% resistance=220 package=THT]
  R9 = Resistor [tolerance=±5% resistance=220 package=THT]
  R10 = Resistor [tolerance=±5% resistance=220 package=THT]
  R11 = Resistor [tolerance=±5% resistance=220 package=THT]
  R12 = Resistor [tolerance=±5% resistance=220 package=THT]
  R13 = Resistor [tolerance=±5% resistance=220 package=THT]
  R14 = Resistor [tolerance=±5% resistance=220 package=THT]
  R15 = Resistor [tolerance=±5% resistance=220 package=THT]
  R16 = Resistor [tolerance=±5% resistance=220 package=THT]
  R17 = Resistor [tolerance=±5% resistance=220 package=THT]

nets:
  N1: Raspberry_Pi1.GPIO2, R13.Pin_0
  N2: Raspberry_Pi1.GPIO3, R14.Pin_0
  N3: Raspberry_Pi1.GPIO4, R15.Pin_0
  GND: Raspberry_Pi1.GND, LED1.common_cathode, LED2.common_cathode, Bauteil1.-, U1.GND, R13.Pin_1, R14.Pin_1, R15.Pin_1, R16.Pin_1, R17.Pin_1
  N4: Raspberry_Pi1.GPIO17, R16.Pin_0
  N5: Raspberry_Pi1.GPIO27, S2.Pin_1, S2.Pin_2
  N6: Raspberry_Pi1.GPIO22, S3.Pin_4
  N7: Raspberry_Pi1.GPIO10, S1.Pin_1, S1.Pin_2
  N8: Raspberry_Pi1.GPIO9, S4.Pin_1, S4.Pin_2
  N9: Raspberry_Pi1.GPIO26, Bauteil1.S, R17.Pin_0
  N10: Raspberry_Pi1.GPIO21, R5.Pin_0
  N11: Raspberry_Pi1.GPIO20, R4.Pin_0
  N12: Raspberry_Pi1.GPIO16, R6.Pin_0
  N13: Raspberry_Pi1.GPIO12, R8.Pin_0
  N14: Raspberry_Pi1.GPIO25, R10.Pin_0
  N15: Raspberry_Pi1.GPIO24, R12.Pin_0
  5V: Raspberry_Pi1.5V, S1.Pin_3, S1.Pin_4, S2.Pin_3, S2.Pin_4, S3.Pin_1, S4.Pin_3, S4.Pin_4, Bauteil1.+, U1.VDD, Q4.E, Q5.E, Q6.E, R1.Pin_0, R2.Pin_0, R3.Pin_0
  N16: LED1.red_anode, Q1.C
  N17: LED1.green_anode, Q3.C
  N18: LED1.blue_anode, Q2.C
  N19: LED2.red_anode, R7.Pin_1
  N20: LED2.green_anode, R11.Pin_1
  N21: LED2.blue_anode, R9.Pin_1
  N22: Q1.E, R1.Pin_1
  N23: Q1.B, R5.Pin_1
  N24: Q2.E, R2.Pin_1
  N25: Q2.B, R4.Pin_1
  N26: Q3.E, R3.Pin_1
  N27: Q3.B, R6.Pin_1
  N28: Q4.B, R8.Pin_1
  N29: Q4.C, R7.Pin_0
  N30: Q5.B, R10.Pin_1
  N31: Q5.C, R9.Pin_0
  N32: Q6.B, R12.Pin_1
  N33: Q6.C, R11.Pin_0
